# Fritzing sketch Gambar Rangkaian (saved by Fritzing 0.9.5d)

parts:
  A1 = DORHEA ESP32 GPIO breakout board 30pin
  M1 = DOIT Esp32 DevKit v1 (30 pins long, 11 pins width) [part_number=ESP32S-PIN30]  # not connected
  Part1 = 4x Matrix LED 8x8 with MAX7219 [part_number=FC-16]

nets:
  N1: A1.Pin_27, A1.Pin_57, A1.Pin_58, Part1.GND
  N2: A1.Pin_61, A1.Pin_62, Part1.VCC
  N3: A1.Pin_120, Part1.CS
  N4: A1.Pin_121, Part1.CLK
  N5: A1.Pin_127, Part1.DIN

notes:
  Dot Matrix - ESP32
  VCC - 3.3V
  GND - GND
  DIN - D23
  CS - D5
  CLK - D18
  By. Ajang Rahmat
  Kelas Robot

custom parts:
  DORHEA ESP32 GPIO breakout board 30pin: ESP32 shield 30P expansion board, supports two power supply : DC 6.5-16v and USB 5.V
  DOIT Esp32 DevKit v1 (30 pins long, 11 pins width): The DOIT Esp32 DevKit v1 is one of the development board created by DOIT to evaluate the ESP-WROOM-32 module. It is based on the ESP32 microcontroller that boasts Wifi, Bluetooth, Ethernet and Low Power support all in a single chip. (vanepp) made breadboard work, adjusted pin numbering and labels and reduced size of schematic and cleaned up pcb. This chip is 30pins long (2 x15) and 11 pins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
  4x Matrix LED 8x8 with MAX7219: FC-16
